// Logisim project Advanced_Features.circ as structural Verilog: 1 circuit, main circuit main
module main (
  input  in_1,
  output [5:0] out_2
);

  wire [15:0] bit_extender_1_out;

  // Probe on 4'b1001
  // Probe on 2'b01
  // Probe on 2'b10
  assign bit_extender_1_out = {{8{1'b0}}, {8{1'b1}}};  // Bit_Extender bit_extender_1
  // Probe on 2'b11
  // Probe on in_1
  // Probe on bit_extender_1_out

  assign out_2 = 6'b111001;

  // Other names for the same wires on the sheet: sig = in_1
endmodule
